# Fritzing sketch schema-arduino-fritzing (saved by Fritzing 0.9.2b)

parts:
  Part1 = Arduino Mega 2560 (Rev3)
  Part2 = Arduino Ethernet Shield (Rev3)
  LCD1 = LCD screen
  DHT1 = DHT22 Humidity and Temperature Sensor
  R1 = Resistor [tolerance=±5% resistance=220 package=THT]
  R2 = Rotary Potentiometer (Large) [maximum_resistance=100kΩ package=THT]

nets:
  5V: Part1.5V, LCD1.VDD, LCD1.LED+, R2.leg1
  N1: Part1.D23, LCD1.RS
  N2: Part1.D25, LCD1.E
  N3: Part1.D27, LCD1.DB4
  N4: Part1.D29, LCD1.DB5
  N5: Part1.D31, LCD1.DB6
  N6: Part1.D33, LCD1.DB7
  N7: Part1.D53, DHT1.DATA, R1.Pin_0
  GND: Part1.GND, LCD1.VSS, LCD1.R/W, LCD1.LED-, R2.leg2
  5V_2: Part2.5V, DHT1.VDD, R1.Pin_1
  GND_2: Part2.GND, DHT1.GND
  N8: LCD1.V0, R2.wiper

notes:
  Pins 10, 11, 12, 13 on the Arduino Ethernet Shield are used, do not use them + The SD card takes pin 4 on the Arduino Ethernet Shield
